# Fritzing sketch scheme (saved by Fritzing 0.9.2b)
breadboards: 1

parts:
  Часть1 = Arduino Uno (Rev3)
  Raspberry_Pi1 = Raspberry Pi 2
  R1 = Rotary Potentiometer (Small) [maximum_resistance=100kΩ package=THT]
  R2 = Photocell (LDR) [package=THT]
  S1 = Pushbutton [package="[THT]"]
  R3 = Resistor [tolerance=±5% resistance=10k package=THT]
  R4 = Resistor [tolerance=±5% resistance=10k package=THT]
  R5 = Resistor [tolerance=±5% resistance=220 package=THT]
  R6 = Resistor [tolerance=±5% resistance=220 package=THT]
  R7 = Resistor [tolerance=±5% resistance=220 package=THT]
  LED3 = LED - 5mm [color="Red (633nm)" package="5 mm [THT]"]
  LED4 = LED - 5mm [color="Red (633nm)" package="5 mm [THT]"]
  LED5 = LED - 5mm [color="Red (633nm)" package="5 mm [THT]"]
  Q1 = Basic FET P-Channel [package="TO220 [THT]"]
  R8 = Resistor [tolerance=±5% resistance=220 package=THT]
  R9 = Resistor [tolerance=±5% resistance=220 package=THT]
  R10 = Resistor [tolerance=±5% resistance=220 package=THT]
  K1 = Relay [part_number=FRS1B-S package=THT]
  Power_plug1 = Power plug  # not connected
  X1 = USB Connectors [package=usb-a-h]  # not connected

nets:
  N1: Часть1.A0, R2.pin_1, R4.Pin_1
  N2: Часть1.A1, R1.wiper
  N3: Часть1.A4/SDA, Raspberry_Pi1.GPIO2
  N4: Часть1.A5/SCL, Raspberry_Pi1.GPIO3
  N5: Часть1.D8, S1.Pin_1, S1.Pin_2, R3.Pin_1
  N6: Часть1.D10_PWM/SS, R7.Pin_0
  N7: Часть1.D11_PWM/MOSI, R6.Pin_0
  N8: Часть1.D12/MISO, R5.Pin_0
  N9: Часть1.D7, R8.Pin_0, R9.Pin_0, R10.Pin_0
  N10: Часть1.5V, R1.leg1, R2.pin_0, S1.Pin_3, S1.Pin_4
  GND: Часть1.GND, Raspberry_Pi1.GND, R1.leg2, R3.Pin_0, R4.Pin_0, LED3.cathode, LED4.cathode, LED5.cathode, Q1.source
  N11: Часть1.VIN, K1.COIL1
  N12: R5.Pin_1, LED5.anode
  N13: R6.Pin_1, LED4.anode
  N14: R7.Pin_1, LED3.anode
  N15: Q1.gate, R8.Pin_1, R9.Pin_1, R10.Pin_1
  N16: Q1.drain, K1.COIL2

notes:
  USB modem ZTE MF831
  DC power supply 5V 2A
  connect the camera
